# Fritzing sketch LDR Servo Schematic (saved by Fritzing 0.9.3b)
breadboards: 1

parts:
  Nino = Arduino Uno (Rev3)
  J1 = Basic Servo
  R1 = Photocell (LDR) [package=THT]
  R2 = Photocell (LDR) [package=THT]
  R3 = Resistor [tolerance=±5% resistance=1k package="0603 [SMD]"]
  R4 = Resistor [tolerance=±5% resistance=1k package="0603 [SMD]"]

nets:
  N1: Nino.A0, R1.pin_0, R4.Pin_1
  N2: Nino.A1, R2.pin_0, R3.Pin_1
  N3: Nino.D9_PWM, J1.pulse
  GND: Nino.GND, J1.gnd, R3.Pin_0, R4.Pin_0
  5V: Nino.5V, J1.vcc, R1.pin_1
