# Fritzing sketch Succulent Fritzing (saved by Fritzing 0.9.3b)
breadboards: 1

parts:
  Nino_Panes_-_Succulent_Planter = Arduino Uno (Rev3)
  part = H-Bridge [package=THT]
  M1 = DC Motor
  M2 = DC Motor
  R1 = Photocell (LDR) [package=THT]
  R2 = Photocell (LDR) [package=THT]
  R3 = Photocell (LDR) [package=THT]
  R4 = Photocell (LDR) [package=THT]
  R5 = Resistor [tolerance=±5% resistance=220 package="2010 [SMD]"]
  R6 = Resistor [tolerance=±5% resistance=220 package="2010 [SMD]"]
  R7 = Resistor [tolerance=±5% resistance=220 package="2010 [SMD]"]
  R8 = Resistor [tolerance=±5% resistance=220 package="2010 [SMD]"]
  S1 = Momentary Switch [package=tactile-pth]
  R9 = Resistor [tolerance=±5% resistance=10k package=THT]

nets:
  N1: Nino_Panes_-_Succulent_Planter.A0, R1.pin_1
  N2: Nino_Panes_-_Succulent_Planter.A1, R2.pin_1
  N3: Nino_Panes_-_Succulent_Planter.A2, R3.pin_1
  N4: Nino_Panes_-_Succulent_Planter.A3, R4.pin_1
  N5: Nino_Panes_-_Succulent_Planter.D8, part.3_4EN
  N6: Nino_Panes_-_Succulent_Planter.D12/MISO, S1.1
  GND: Nino_Panes_-_Succulent_Planter.GND, part.GND1, part.GND2, part.GND3, part.GND4, R5.Pin_0, R6.Pin_0, R7.Pin_0, R8.Pin_0, R9.Pin_1
  N7: Nino_Panes_-_Succulent_Planter.D2, part.1_2EN
  N8: Nino_Panes_-_Succulent_Planter.D3_PWM, part.1A
  N9: Nino_Panes_-_Succulent_Planter.D4, part.2A
  N10: Nino_Panes_-_Succulent_Planter.D6_PWM, part.4A
  N11: Nino_Panes_-_Succulent_Planter.D7, part.3A
  N12: Nino_Panes_-_Succulent_Planter.5V, part.VCC2, part.VCC1
  N13: part.1Y, M2.pin_1
  N14: part.2Y, M2.pin_2
  N15: part.3Y, M1.pin_2
  N16: part.4Y, M1.pin_1
  N17: R1.pin_0, R5.Pin_1
  N18: R2.pin_0, R6.Pin_1
  N19: R3.pin_0, R7.Pin_1
  N20: R4.pin_0, R8.Pin_1
  N21: S1.4, R9.Pin_0
